# Fritzing sketch Stage_2 (saved by Fritzing 0.9.9b)
perfboards: 1

parts:
  J1 = Camdenboss CTB0158-4 [part_number=CTB0158-4 package=THT]
  J2 = Camdenboss CTB0158-4 [part_number=CTB0158-4 package=THT]
  C4 = Electrolytic Capacitor [capacitance=1µF voltage=35V package="100 mil [THT, electrolytic]"]
  Q1 = Basic FET N-Channel [package="TO220 [THT]"]
  C6 = Ceramic Capacitor [capacitance=100nF voltage=35V package="100 mil [THT, multilayer]"]
  C7 = Ceramic Capacitor [capacitance=100nF voltage=35V package="100 mil [THT, multilayer]"]
  IC1 = IC, DIP package, 14 pins [chip_label=LT3724]
  R7 = Resistor [tolerance=±5% power=0.25 resistance=220 package=THT]
  C10 = Ceramic Capacitor [capacitance=100nF voltage=35V package="100 mil [THT, multilayer]"]
  R8 = Resistor [tolerance=±5% power=0.25 resistance=220 package=THT]
  C11 = Electrolytic Capacitor [capacitance=1µF voltage=35V package="100 mil [THT, electrolytic]"]
  R9 = Resistor [tolerance=±5% power=0.25 resistance=1 package=THT]

nets:
  N1: J1.pin1, J1.pin2, IC1.pin10, IC1.pin14, C11.+, R9.Pin_1
  GND: J1.pin3, J1.pin4, J2.pin3, J2.pin4, C4.-, IC1.pin4, C10.0, R8.Pin_0, C11.-
  N2: J2.pin2, C4.+, Q1.source, IC1.pin13, R7.Pin_1
  N3: Q1.gate, IC1.pin11
  N4: Q1.drain, IC1.pin12, R9.Pin_0
  N5: C6.0, IC1.pin8
  N6: C6.1, IC1.pin9
  N7: C7.0, IC1.pin7
  N8: C7.1, IC1.pin6
  N9: IC1.pin1, R7.Pin_0, R8.Pin_1
  N10: IC1.pin5, C10.1
